# Fritzing sketch grow_strip (saved by Fritzing 0.9.3b)
breadboards: 1

parts:
  Part1 = Arduino Nano (Rev3.0) (ICSP)
  R1 = Resistor [tolerance=±5% resistance=470 package="2010 [SMD]"]
  RGB_SMD_LED1 = SMD RGB LED (WS2812) [package=5050]
  C1 = Electrolytic Capacitor [capacitance=999µF voltage=50V package="1010 [SMD, electrolytic]"]
  Power_plug1 = Power plug
  U1 = POT [package=pot_mammoth]

nets:
  N1: Part1.D6, R1.Pin_0
  VCC: Part1.5V, RGB_SMD_LED1.VCC, C1.+, Power_plug1.VCC, U1.E
  N2: Part1.A1, U1.A
  N3: R1.Pin_1, RGB_SMD_LED1.DIn
  VSS: RGB_SMD_LED1.VSS, C1.-, Power_plug1.GND, U1.S

notes:
  50 LEDs in this strip.
  5V 4A
  pot = AnalogRead(1)
  blue = pot / POT_MAX
  red = 1 - blue
  color = RGB(red, 0, blue)
  SetLEDs(/* pin */ 6, color)
